// Logisim project lockkey.circ as structural Verilog: 1 circuit, main circuit main
module main (
  input  in_1
);

  wire and_1_out, button_1_out, button_2_out, comparator_1_eq, comparator_2_eq, or_1_out;
  wire [2:0] counter_1_q;
  wire [3:0] d_ff_1_q;

  Button button_1 (.out(button_1_out));
  Button button_2 (.out(button_2_out));
  D_Flip_Flop d_ff_1 (.D(in_1), .clk(button_2_out), .Q(d_ff_1_q[0]), .reset(button_1_out));  // open: Qn, preset
  D_Flip_Flop d_ff_2 (.D(d_ff_1_q[0]), .clk(button_2_out), .Q(d_ff_1_q[1]), .reset(button_1_out));  // open: Qn, preset
  D_Flip_Flop d_ff_3 (.D(d_ff_1_q[1]), .clk(button_2_out), .Q(d_ff_1_q[2]), .reset(button_1_out));  // open: Qn, preset
  D_Flip_Flop d_ff_4 (.D(d_ff_1_q[2]), .clk(button_2_out), .Q(d_ff_1_q[3]), .reset(button_1_out));  // open: Qn, preset
  Counter #(.max('h7), .width(3)) counter_1 (
    .clr(or_1_out), .up(1'b1), .count(1'b1), .clk(button_2_out), .Q(counter_1_q));  // open: load, D, carry
  Comparator #(.mode("unsigned"), .width(4)) comparator_1 (
    .a(d_ff_1_q), .b(4'b1000), .eq(comparator_1_eq));  // open: gt, lt
  and and_1 (and_1_out, comparator_1_eq, comparator_2_eq);
  LED led_1 (.in(and_1_out));
  Comparator #(.mode("unsigned"), .width(3)) comparator_2 (
    .a(counter_1_q), .b(3'b100), .eq(comparator_2_eq));  // open: gt, lt
  or or_1 (or_1_out, button_1_out, comparator_2_eq);
endmodule
